# Fritzing sketch p2arduino (saved by Fritzing 0.9.3b)
breadboards: 1

parts:
  Part1 = Arduino Uno (Rev3)
  LCD1 = LCD screen
  R1 = Resistor [tolerance=±5% resistance=220 package=THT]
  R2 = Trimmer Potentiometer [maximum_resistance=10kΩ package=THT]
  U1 = HALL-EFFECT [package=sc70]
  R3 = Resistor [tolerance=±5% resistance=220 package=THT]
  S1 = Toggle Switch [package=THT]
  VCC1 = 4 x AAA Battery Mount

nets:
  N1: Part1.D8, R3.Pin_0, S1.L2
  N2: Part1.D11_PWM/MOSI, LCD1.E
  N3: Part1.D12/MISO, LCD1.RS
  N4: Part1.D4, LCD1.DB7
  N5: Part1.D5_PWM, LCD1.DB6
  N6: Part1.D6_PWM, LCD1.DB5
  N7: Part1.D7, LCD1.DB4
  5V: Part1.5V, LCD1.VDD, R1.Pin_1, R2.leg1, S1.COM
  GND: Part1.GND, LCD1.R/W, LCD1.LED-, R2.leg2, U1.GND, R3.Pin_1, VCC1.-
  N8: Part1.VIN, VCC1.+
  N9: LCD1.V0, R2.wiper
  N10: LCD1.LED+, R1.Pin_0
